// Logisim project proiect.circ as structural Verilog
module main (
  input  in_1
);

  wire clock_1_out;
  wire [3:0] convertor_bin_dec_1_uni, convertor_bin_dec_1_zec, convertor_bin_dec_2_uni,
       convertor_bin_dec_2_zec, convertor_bin_dec_an_1_mi, convertor_bin_dec_an_1_sut,
       convertor_bin_dec_an_1_uni, convertor_bin_dec_an_1_zec, convertor_bin_dec_luna_1_uni,
       convertor_bin_dec_luna_1_zec, convertor_bin_dec_ore_1_uni, convertor_bin_dec_ore_1_zec,
       convertor_bin_dec_ore_2_uni, convertor_bin_dec_ore_2_zec, numarator_luna_1_data_luna;
  wire [4:0] numarator_ore_1_ore, numarator_zi_1_data_zi;
  wire [5:0] numarator_minute_1_minute, numarator_secunda_1_secunda;
  wire [6:0] decoder_7segm_1_o, decoder_7segm_2_o, decoder_7segm_3_o, decoder_7segm_4_o, decoder_7segm_5_o,
       decoder_7segm_6_o, decoder_7segm_7_o, decoder_7segm_8_o, decoder_7segm_9_o, decoder_7segm_10_o,
       decoder_7segm_11_o, decoder_7segm_12_o, decoder_7segm_13_o, decoder_7segm_14_o, ziua_litere_1_o,
       ziua_litere_1_o2;
  wire [10:0] numarator_an_1_data_an;

  Clock clock_1 (.out(clock_1_out));
  convertor_bin_dec_ore convertor_bin_dec_ore_1 (
    .bin(numarator_ore_1_ore), .zec(convertor_bin_dec_ore_1_zec), .uni(convertor_bin_dec_ore_1_uni));
  convertor_bin_dec_ore convertor_bin_dec_ore_2 (
    .bin(numarator_zi_1_data_zi), .zec(convertor_bin_dec_ore_2_zec), .uni(convertor_bin_dec_ore_2_uni));
  convertor_bin_dec_luna convertor_bin_dec_luna_1 (
    .bin(numarator_luna_1_data_luna), .zec(convertor_bin_dec_luna_1_zec), .uni(convertor_bin_dec_luna_1_uni));
  convertor_bin_dec_an convertor_bin_dec_an_1 (
    .bin(numarator_an_1_data_an), .mi(convertor_bin_dec_an_1_mi), .sut(convertor_bin_dec_an_1_sut),
    .zec(convertor_bin_dec_an_1_zec), .uni(convertor_bin_dec_an_1_uni));
  numarator_secunda numarator_secunda_1 (.clk(clock_1_out), .enable(in_1), .secunda(numarator_secunda_1_secunda));
  convertor_bin_dec convertor_bin_dec_1 (
    .bin(numarator_minute_1_minute), .zec(convertor_bin_dec_1_zec), .uni(convertor_bin_dec_1_uni));
  decoder_7segm decoder_7segm_1 (.i(convertor_bin_dec_1_zec), .o(decoder_7segm_1_o));
  decoder_7segm decoder_7segm_2 (.i(convertor_bin_dec_1_uni), .o(decoder_7segm_2_o));
  decoder_7segm decoder_7segm_3 (.i(convertor_bin_dec_ore_1_zec), .o(decoder_7segm_3_o));
  decoder_7segm decoder_7segm_4 (.i(convertor_bin_dec_ore_1_uni), .o(decoder_7segm_4_o));
  decoder_7segm decoder_7segm_5 (.i(convertor_bin_dec_ore_2_zec), .o(decoder_7segm_5_o));
  decoder_7segm decoder_7segm_6 (.i(convertor_bin_dec_ore_2_uni), .o(decoder_7segm_6_o));
  decoder_7segm decoder_7segm_7 (.i(convertor_bin_dec_luna_1_zec), .o(decoder_7segm_7_o));
  decoder_7segm decoder_7segm_8 (.i(convertor_bin_dec_luna_1_uni), .o(decoder_7segm_8_o));
  numarator_minute numarator_minute_1 (
    .clk(clock_1_out), .semnal(numarator_secunda_1_secunda), .enable(in_1), .minute(numarator_minute_1_minute));
  _7_Segment_Display u_7_segment_display_1 (
    .g(decoder_7segm_1_o[0]), .f(decoder_7segm_1_o[1]), .a(decoder_7segm_1_o[6]), .b(decoder_7segm_1_o[5]),
    .e(decoder_7segm_1_o[2]), .d(decoder_7segm_1_o[3]), .c(decoder_7segm_1_o[4]));  // open: dp
  decoder_7segm decoder_7segm_9 (.i(convertor_bin_dec_an_1_mi), .o(decoder_7segm_9_o));
  decoder_7segm decoder_7segm_10 (.i(convertor_bin_dec_an_1_sut), .o(decoder_7segm_10_o));
  decoder_7segm decoder_7segm_11 (.i(convertor_bin_dec_an_1_zec), .o(decoder_7segm_11_o));
  decoder_7segm decoder_7segm_12 (.i(convertor_bin_dec_an_1_uni), .o(decoder_7segm_12_o));
  _7_Segment_Display u_7_segment_display_2 (
    .g(decoder_7segm_2_o[0]), .f(decoder_7segm_2_o[1]), .a(decoder_7segm_2_o[6]), .b(decoder_7segm_2_o[5]),
    .e(decoder_7segm_2_o[2]), .d(decoder_7segm_2_o[3]), .c(decoder_7segm_2_o[4]));  // open: dp
  numarator_ore numarator_ore_1 (
    .clk(clock_1_out), .enable(in_1), .semnal_secunde(numarator_secunda_1_secunda),
    .semnal_minute(numarator_minute_1_minute), .ore(numarator_ore_1_ore));
  _7_Segment_Display u_7_segment_display_3 (
    .g(decoder_7segm_4_o[0]), .f(decoder_7segm_4_o[1]), .a(decoder_7segm_4_o[6]), .b(decoder_7segm_4_o[5]),
    .e(decoder_7segm_4_o[2]), .d(decoder_7segm_4_o[3]), .c(decoder_7segm_4_o[4]));  // open: dp
  _7_Segment_Display u_7_segment_display_4 (
    .g(decoder_7segm_3_o[0]), .f(decoder_7segm_3_o[1]), .a(decoder_7segm_3_o[6]), .b(decoder_7segm_3_o[5]),
    .e(decoder_7segm_3_o[2]), .d(decoder_7segm_3_o[3]), .c(decoder_7segm_3_o[4]));  // open: dp
  _7_Segment_Display u_7_segment_display_5 (
    .g(decoder_7segm_5_o[0]), .f(decoder_7segm_5_o[1]), .a(decoder_7segm_5_o[6]), .b(decoder_7segm_5_o[5]),
    .e(decoder_7segm_5_o[2]), .d(decoder_7segm_5_o[3]), .c(decoder_7segm_5_o[4]));  // open: dp
  numarator_zi numarator_zi_1 (
    .clk(clock_1_out), .enable(in_1), .semnal_sec(numarator_secunda_1_secunda),
    .semnal_min(numarator_minute_1_minute), .semnal_ore(numarator_ore_1_ore), .data_zi(numarator_zi_1_data_zi));
  _7_Segment_Display u_7_segment_display_6 (
    .g(decoder_7segm_6_o[0]), .f(decoder_7segm_6_o[1]), .a(decoder_7segm_6_o[6]), .b(decoder_7segm_6_o[5]),
    .e(decoder_7segm_6_o[2]), .d(decoder_7segm_6_o[3]), .c(decoder_7segm_6_o[4]));  // open: dp
  _7_Segment_Display u_7_segment_display_7 (
    .g(decoder_7segm_7_o[0]), .f(decoder_7segm_7_o[1]), .a(decoder_7segm_7_o[6]), .b(decoder_7segm_7_o[5]),
    .e(decoder_7segm_7_o[2]), .d(decoder_7segm_7_o[3]), .c(decoder_7segm_7_o[4]));  // open: dp
  _7_Segment_Display u_7_segment_display_8 (
    .g(decoder_7segm_8_o[0]), .f(decoder_7segm_8_o[1]), .a(decoder_7segm_8_o[6]), .b(decoder_7segm_8_o[5]),
    .e(decoder_7segm_8_o[2]), .d(decoder_7segm_8_o[3]), .c(decoder_7segm_8_o[4]));  // open: dp
  numarator_luna numarator_luna_1 (
    .clk(clock_1_out), .enable(in_1), .semnal_sec(numarator_secunda_1_secunda),
    .semnal_min(numarator_minute_1_minute), .semnal_ore(numarator_ore_1_ore),
    .semnal_data_zi(numarator_zi_1_data_zi), .data_luna(numarator_luna_1_data_luna));
  _7_Segment_Display u_7_segment_display_9 (
    .g(decoder_7segm_9_o[0]), .f(decoder_7segm_9_o[1]), .a(decoder_7segm_9_o[6]), .b(decoder_7segm_9_o[5]),
    .e(decoder_7segm_9_o[2]), .d(decoder_7segm_9_o[3]), .c(decoder_7segm_9_o[4]));  // open: dp
  _7_Segment_Display u_7_segment_display_10 (
    .g(decoder_7segm_10_o[0]), .f(decoder_7segm_10_o[1]), .a(decoder_7segm_10_o[6]),
    .b(decoder_7segm_10_o[5]), .e(decoder_7segm_10_o[2]), .d(decoder_7segm_10_o[3]), .c(decoder_7segm_10_o[4]));  // open: dp
  _7_Segment_Display u_7_segment_display_11 (
    .g(decoder_7segm_11_o[0]), .f(decoder_7segm_11_o[1]), .a(decoder_7segm_11_o[6]),
    .b(decoder_7segm_11_o[5]), .e(decoder_7segm_11_o[2]), .d(decoder_7segm_11_o[3]), .c(decoder_7segm_11_o[4]));  // open: dp
  _7_Segment_Display u_7_segment_display_12 (
    .g(decoder_7segm_12_o[0]), .f(decoder_7segm_12_o[1]), .a(decoder_7segm_12_o[6]),
    .b(decoder_7segm_12_o[5]), .e(decoder_7segm_12_o[2]), .d(decoder_7segm_12_o[3]), .c(decoder_7segm_12_o[4]));  // open: dp
  numarator_an numarator_an_1 (
    .clk(clock_1_out), .enable(in_1), .semnal_sec(numarator_secunda_1_secunda),
    .semnal_min(numarator_minute_1_minute), .semnal_ore(numarator_ore_1_ore),
    .semnal_data_zi(numarator_zi_1_data_zi), .semnal_data_luna(numarator_luna_1_data_luna),
    .data_an(numarator_an_1_data_an));
  _7_Segment_Display u_7_segment_display_13 (
    .g(ziua_litere_1_o[0]), .f(ziua_litere_1_o[1]), .a(ziua_litere_1_o[6]), .b(ziua_litere_1_o[5]),
    .e(ziua_litere_1_o[2]), .d(ziua_litere_1_o[3]), .c(ziua_litere_1_o[4]));  // open: dp
  _7_Segment_Display u_7_segment_display_14 (
    .g(ziua_litere_1_o2[0]), .f(ziua_litere_1_o2[1]), .a(ziua_litere_1_o2[6]), .b(ziua_litere_1_o2[5]),
    .e(ziua_litere_1_o2[2]), .d(ziua_litere_1_o2[3]), .c(ziua_litere_1_o2[4]));  // open: dp
  convertor_bin_dec convertor_bin_dec_2 (
    .bin(numarator_secunda_1_secunda), .zec(convertor_bin_dec_2_zec), .uni(convertor_bin_dec_2_uni));
  decoder_7segm decoder_7segm_13 (.i(convertor_bin_dec_2_zec), .o(decoder_7segm_13_o));
  decoder_7segm decoder_7segm_14 (.i(convertor_bin_dec_2_uni), .o(decoder_7segm_14_o));
  ziua_litere ziua_litere_1 (
    .clk(clock_1_out), .ora(numarator_ore_1_ore), .min(numarator_minute_1_minute),
    .sec(numarator_secunda_1_secunda), .o(ziua_litere_1_o), .o2(ziua_litere_1_o2));
  _7_Segment_Display u_7_segment_display_15 (
    .g(decoder_7segm_13_o[0]), .f(decoder_7segm_13_o[1]), .a(decoder_7segm_13_o[6]),
    .b(decoder_7segm_13_o[5]), .e(decoder_7segm_13_o[2]), .d(decoder_7segm_13_o[3]), .c(decoder_7segm_13_o[4]));  // open: dp
  _7_Segment_Display u_7_segment_display_16 (
    .g(decoder_7segm_14_o[0]), .f(decoder_7segm_14_o[1]), .a(decoder_7segm_14_o[6]),
    .b(decoder_7segm_14_o[5]), .e(decoder_7segm_14_o[2]), .d(decoder_7segm_14_o[3]), .c(decoder_7segm_14_o[4]));  // open: dp
endmodule

// VHDL entity numarator_secunda, as the project stores it:
LIBRARY ieee;
USE ieee.std_logic_1164.all;
use ieee.std_logic_unsigned.all;
use IEEE.NUMERIC_STD.ALL;

ENTITY numarator_secunda IS
  PORT (
  	clk: in std_logic;
  	enable: in std_logic;
  	secunda: out std_logic_vector(5 downto 0)

  	);
END numarator_secunda;


ARCHITECTURE TypeArchitecture OF numarator_secunda IS

signal count_secunda: unsigned(5 downto 0):="000000";

BEGIN
process(clk)
begin
	if enable='1' then
		if rising_edge(clk) then
				if count_secunda=59 then
					count_secunda<="000000";
				else
					count_secunda<=count_secunda+1;
				end if;
		end if;
	end if;
end process;

secunda<=std_logic_vector(count_secunda);

END TypeArchitecture;

// VHDL entity numarator_minute, as the project stores it:
LIBRARY ieee;
USE ieee.std_logic_1164.all;
use ieee.std_logic_unsigned.all;
use IEEE.NUMERIC_STD.ALL;

ENTITY numarator_minute IS
  PORT (clk:in std_logic;
  	   semnal: in std_logic_vector(5 downto 0);
  	   enable: in std_logic;
  	   minute: out std_logic_vector(5 downto 0));
  	   
END numarator_minute;
 	
ARCHITECTURE TypeArchitecture OF numarator_minute IS

signal count_minut: unsigned(5 downto 0):="111011";

BEGIN
process(clk)
begin
	if enable='1' then
		if rising_edge(clk) then
			if count_minut=59 then
				if semnal=59 then
					count_minut<="000000";
				end if;
			elsif semnal=59 then
				count_minut<=count_minut+1;
			end if;
		end if;
	end if;
end process;
minute<=std_logic_vector(count_minut);
END TypeArchitecture;

// VHDL entity numarator_ore, as the project stores it:
LIBRARY ieee;
USE ieee.std_logic_1164.all;
use ieee.std_logic_unsigned.all;
use IEEE.NUMERIC_STD.ALL;

ENTITY numarator_ore IS
  PORT (clk:in std_logic;
  	   enable: in std_logic;
  	   semnal_secunde: in std_logic_vector(5 downto 0);
  	   semnal_minute: in std_logic_vector(5 downto 0);
  	   ore: out std_logic_vector(4 downto 0));
  	   
END numarator_ore;
 	
ARCHITECTURE TypeArchitecture OF numarator_ore IS

signal count_ore: unsigned(4 downto 0):="10111";

BEGIN

process(clk)

begin
	if enable='1' then
		if rising_edge(clk) then
			if count_ore=23 then
				if semnal_minute=59 then
					if semnal_secunde=59 then
						count_ore<="00000";
					end if;
				end if;
			elsif semnal_minute=59 then
				if semnal_secunde=59 then
					count_ore<=count_ore+1;
				end if;
			end if;
		end if;
	end if;
end process;
ore<=std_logic_vector(count_ore);
END TypeArchitecture;

// VHDL entity numarator_zi, as the project stores it:
LIBRARY ieee;
USE ieee.std_logic_1164.all;
use ieee.std_logic_unsigned.all;
use IEEE.NUMERIC_STD.ALL;

ENTITY numarator_zi IS
  PORT (clk:in std_logic;
        enable:in std_logic;
        semnal_sec:in std_logic_vector(5 downto 0);
        semnal_min:in std_logic_vector(5 downto 0);
        semnal_ore:in std_logic_vector(4 downto 0);
        data_zi:out std_logic_vector(4 downto 0));
        
END numarator_zi;

ARCHITECTURE TypeArchitecture OF numarator_zi IS

signal count_data_zi: unsigned(4 downto 0):="11101";

BEGIN

process(clk)
begin
	if enable='1' then
		if rising_edge(clk) then
			if count_data_zi=29 then
				if semnal_ore=23 then
					if semnal_min=59 then
						if semnal_sec=59 then
							count_data_zi<="00001";
						end if;
					end if;
				end if;
			elsif semnal_ore=23 then
				if semnal_min=59 then
					if semnal_sec=59 then
						count_data_zi<=count_data_zi+1;
					end if;
				end if;
			end if;
		end if;
	end if;
end process;

data_zi<=std_logic_vector(count_data_zi);
END TypeArchitecture;

// VHDL entity numarator_luna, as the project stores it:
LIBRARY ieee;
USE ieee.std_logic_1164.all;
use ieee.std_logic_unsigned.all;
use IEEE.NUMERIC_STD.ALL;

ENTITY numarator_luna IS
  PORT (clk:in std_logic;
        enable:in std_logic;
        semnal_sec:in std_logic_vector(5 downto 0);
        semnal_min:in std_logic_vector(5 downto 0);
        semnal_ore:in std_logic_vector(4 downto 0);
        semnal_data_zi:in std_logic_vector(4 downto 0);
        data_luna:out std_logic_vector(3 downto 0));
        
        
END numarator_luna;

ARCHITECTURE TypeArchitecture OF numarator_luna IS

signal count_data_luna: unsigned(3 downto 0):="1011";

BEGIN

process(clk)

begin
	if enable='1' then
		if rising_edge(clk) then
			if count_data_luna=12 then
				if semnal_data_zi=30 then
					if semnal_ore=23 then
						if semnal_min=59 then
							if semnal_sec=59 then
								count_data_luna<="0001";
							end if;
						end if;
					end if;
				end if;
			elsif semnal_data_zi=29 then
					if semnal_ore=23 then
						if semnal_min=59 then
							if semnal_sec=59 then
								count_data_luna<=count_data_luna+1;
							end if;
						end if;
					end if;
			end if;
		end if;
	end if;
				
end process;

data_luna<=std_logic_vector(count_data_luna);
END TypeArchitecture;

// VHDL entity numarator_an, as the project stores it:
LIBRARY ieee;
USE ieee.std_logic_1164.all;
use ieee.std_logic_unsigned.all;
use IEEE.NUMERIC_STD.ALL;

ENTITY numarator_an IS
  PORT (clk:in std_logic;
        enable:in std_logic;
        semnal_sec:in std_logic_vector(5 downto 0);
        semnal_min:in std_logic_vector(5 downto 0);
        semnal_ore:in std_logic_vector(4 downto 0);
        semnal_data_zi:in std_logic_vector(4 downto 0);
        semnal_data_luna:in std_logic_vector(3 downto 0);
        data_an:out std_logic_vector(10 downto 0));
        
        
END numarator_an;

ARCHITECTURE TypeArchitecture OF numarator_an IS

signal count_data_an: unsigned(10 downto 0):="11111100111";

BEGIN

process(clk)

begin
	if enable='1' then
		if rising_edge(clk) then
			if semnal_data_luna=12 then
				if semnal_data_zi=29 then
					if semnal_ore=23 then
						if semnal_min=59 then
							if semnal_sec=59 then
								count_data_an<=count_data_an+1;
							end if;
						end if;
					end if;
				end if;
			end if;
		end if;
	end if;
				
end process;

data_an<=std_logic_vector(count_data_an);
END TypeArchitecture;

// VHDL entity alarma, as the project stores it:
LIBRARY ieee;
USE ieee.std_logic_1164.all;
use ieee.std_logic_unsigned.all;
use IEEE.NUMERIC_STD.ALL;
ENTITY alarma IS
  PORT (minute_alarma: in std_logic_vector(5 downto 0);
  	   ora_alarma: in std_logic_vector(4 downto 0);
  	   minute: in std_logic_vector(5 downto 0);
  	   ora: in std_logic_vector(4 downto 0);
  	   suna_alarma: out std_logic_vector(1 downto 0));
  	   
END alarma;

ARCHITECTURE TypeArchitecture OF alarma IS

signal alarm: unsigned(1 downto 0):="00";
signal numar_ora_alarma:integer:=0;
signal numar_ora:integer:=0;
signal numar_minute_alarma:integer:=0;
signal numar_minute:integer:=0;

BEGIN

numar_ora_alarma<=conv_integer(ora_alarma);
numar_ora<=conv_integer(ora);
numar_minute_alarma<=conv_integer(minute_alarma);
numar_minute<=conv_integer(minute);

process(minute_alarma,ora_alarma,minute,ora)

begin
if numar_minute_alarma = numar_minute then
	if numar_ora_alarma = numar_ora then
		alarm<="11";
	else
		alarm<="00";
	end if;
else
	alarm<="00";
end if;

end process;

suna_alarma<=std_logic_vector(alarm);
END TypeArchitecture;

// VHDL entity convertor_bin_dec, as the project stores it:
LIBRARY ieee;
USE ieee.std_logic_1164.all;
use ieee.std_logic_unsigned.all;
use ieee.std_logic_arith.all;

ENTITY convertor_bin_dec IS
  PORT (bin:in std_logic_vector(5 downto 0);
  	   zec:out std_logic_vector(3 downto 0);
  	   uni:out std_logic_vector(3 downto 0));
END convertor_bin_dec;


ARCHITECTURE TypeArchitecture OF convertor_bin_dec IS

signal numar:integer:=0;
signal z,u:integer:=0;

BEGIN

numar<=conv_integer(bin);
z<=numar/10;
u<=numar rem 10;

process(z)
begin
	case z is
		when 0 => zec <=x"0";
		when 1 => zec <=x"1";
		when 2 => zec <=x"2";
		when 3 => zec <=x"3";
		when 4 => zec <=x"4";
		when 5 => zec <=x"5";
		when 6 => zec <=x"6";
		when 7 => zec <=x"7";
		when 8 => zec <=x"8";
		when 9 => zec <=x"9";
		when others => zec <=x"f";
	end case;
end process;

process(u)
begin
	case u is
		when 0 => uni <=x"0";
		when 1 => uni <=x"1";
		when 2 => uni <=x"2";
		when 3 => uni <=x"3";
		when 4 => uni <=x"4";
		when 5 => uni <=x"5";
		when 6 => uni <=x"6";
		when 7 => uni <=x"7";
		when 8 => uni <=x"8";
		when 9 => uni <=x"9";
		when others => uni <=x"f";
	end case;
end process;
	

END TypeArchitecture;

// VHDL entity decoder_7segm, as the project stores it:
LIBRARY ieee;
USE ieee.std_logic_1164.all;

ENTITY decoder_7segm IS
  PORT (i: in std_logic_vector(3 downto 0);
  	   o: out std_logic_vector(6 downto 0));
END decoder_7segm;


ARCHITECTURE TypeArchitecture OF decoder_7segm IS

BEGIN
process(i)
begin
	if (i="0000") then
		o<="1111110";
	elsif (i="0001") then
		o<="0110000";
	elsif (i="0010") then
		o<="1101101";
	elsif (i="0011") then
		o<="1111001";
	elsif (i="0100") then
		o<="0110011";
	elsif (i="0101") then
		o<="1011011";
	elsif (i="0110") then
		o<="1011111";
	elsif (i="0111") then
		o<="1110000";
	elsif (i="1000") then
		o<="1111111";
	elsif (i="1001") then
		o<="1111011";
	end if;
end process;
END TypeArchitecture;

// VHDL entity convertor_bin_dec_luna, as the project stores it:
LIBRARY ieee;
USE ieee.std_logic_1164.all;
use ieee.std_logic_unsigned.all;
use ieee.std_logic_arith.all;

ENTITY convertor_bin_dec_luna IS
  PORT (
bin:in std_logic_vector(3 downto 0);
  	   zec:out std_logic_vector(3 downto 0);
  	   uni:out std_logic_vector(3 downto 0));
END convertor_bin_dec_luna;


ARCHITECTURE TypeArchitecture OF convertor_bin_dec_luna IS

signal numar:integer:=0;
signal z,u:integer:=0;

BEGIN

numar<=conv_integer(bin);
z<=numar/10;
u<=numar rem 10;

process(z)
begin
	case z is
		when 0 => zec <=x"0";
		when 1 => zec <=x"1";
		when 2 => zec <=x"2";
		when 3 => zec <=x"3";
		when 4 => zec <=x"4";
		when 5 => zec <=x"5";
		when 6 => zec <=x"6";
		when 7 => zec <=x"7";
		when 8 => zec <=x"8";
		when 9 => zec <=x"9";
		when others => zec <=x"f";
	end case;
end process;

process(u)
begin
	case u is
		when 0 => uni <=x"0";
		when 1 => uni <=x"1";
		when 2 => uni <=x"2";
		when 3 => uni <=x"3";
		when 4 => uni <=x"4";
		when 5 => uni <=x"5";
		when 6 => uni <=x"6";
		when 7 => uni <=x"7";
		when 8 => uni <=x"8";
		when 9 => uni <=x"9";
		when others => uni <=x"f";
	end case;
end process;
	

END TypeArchitecture;

// VHDL entity convertor_bin_dec_an, as the project stores it:
LIBRARY ieee;
USE ieee.std_logic_1164.all;
use ieee.std_logic_unsigned.all;
use ieee.std_logic_arith.all;

ENTITY convertor_bin_dec_an IS
  PORT (
bin:in std_logic_vector(10 downto 0);
	   mi:out std_logic_vector(3 downto 0);
	   sut:out std_logic_vector(3 downto 0);
  	   zec:out std_logic_vector(3 downto 0);
  	   uni:out std_logic_vector(3 downto 0));
END convertor_bin_dec_an;


ARCHITECTURE TypeArchitecture OF convertor_bin_dec_an IS

signal numar:integer:=0;
signal m,s,z,u:integer:=0;

BEGIN

numar<=conv_integer(bin);
m<=numar/10/10/10;
s<=numar/10 /10 rem 10;
z<=numar/10 rem 10;
u<=numar rem 10;


process(m)
begin
	case m is
		when 0 => mi <=x"0";
		when 1 => mi <=x"1";
		when 2 => mi <=x"2";
		when 3 => mi <=x"3";
		when 4 => mi <=x"4";
		when 5 => mi <=x"5";
		when 6 => mi <=x"6";
		when 7 => mi <=x"7";
		when 8 => mi <=x"8";
		when 9 => mi <=x"9";
		when others => mi <=x"f";
	end case;
end process;

process(s)
begin
	case s is
		when 0 => sut <=x"0";
		when 1 => sut <=x"1";
		when 2 => sut <=x"2";
		when 3 => sut <=x"3";
		when 4 => sut <=x"4";
		when 5 => sut <=x"5";
		when 6 => sut <=x"6";
		when 7 => sut <=x"7";
		when 8 => sut <=x"8";
		when 9 => sut <=x"9";
		when others => sut <=x"f";
	end case;
end process;


process(z)
begin
	case z is
		when 0 => zec <=x"0";
		when 1 => zec <=x"1";
		when 2 => zec <=x"2";
		when 3 => zec <=x"3";
		when 4 => zec <=x"4";
		when 5 => zec <=x"5";
		when 6 => zec <=x"6";
		when 7 => zec <=x"7";
		when 8 => zec <=x"8";
		when 9 => zec <=x"9";
		when others => zec <=x"f";
	end case;
end process;

process(u)
begin
	case u is
		when 0 => uni <=x"0";
		when 1 => uni <=x"1";
		when 2 => uni <=x"2";
		when 3 => uni <=x"3";
		when 4 => uni <=x"4";
		when 5 => uni <=x"5";
		when 6 => uni <=x"6";
		when 7 => uni <=x"7";
		when 8 => uni <=x"8";
		when 9 => uni <=x"9";
		when others => uni <=x"f";
	end case;
end process;
	

END TypeArchitecture;

// VHDL entity ziua_litere, as the project stores it:
LIBRARY ieee;
USE ieee.std_logic_1164.all;
use ieee.std_logic_unsigned.all;
use IEEE.NUMERIC_STD.ALL;

ENTITY ziua_litere IS
  PORT (clk:in std_logic;
  	   ora:in std_logic_vector(4 downto 0);
  	   min:in std_logic_vector(5 downto 0);
  	   sec:in std_logic_vector(5 downto 0);
  	   o:out std_logic_vector(6 downto 0);
  	   o2:out std_logic_vector(6 downto 0));
  	  
END ziua_litere;



ARCHITECTURE TypeArchitecture OF ziua_litere IS

signal zi: unsigned(6 downto 0):="0001110";
signal zi2: unsigned(6 downto 0):="0111110";

BEGIN
process(clk)
begin
	if rising_edge(clk) then
		if ora=23 then
			if min=59 then
				if sec=59 then
					if (zi="0001110") then
						zi<="0110111";
						zi2<="1110111";
					elsif (zi="0110111") then
						if (zi2="1110111") then
						zi<="0110111";
						zi2<="0000110";
						end if;
					elsif (zi="0110111") then
						zi<="0111000";
						zi2<="1111110";
					elsif (zi="0111000") then
						zi<="0011100";
						zi2<="0000010";
					elsif (zi="0011100") then
						zi<="1011011";
						zi2<="1110111";
					elsif (zi="1011011") then
						zi<="1111110";
						zi2<="0111110";
					elsif (zi="1111110") then
						zi<="0001110";
						zi2<="0111110";
					end if;
				end if;
			end if;
		end if;
	end if;
end process;

o<=std_logic_vector(zi);
o2<=std_logic_vector(zi2);
END TypeArchitecture;

// VHDL entity convertor_bin_dec_ore, as the project stores it:
LIBRARY ieee;
USE ieee.std_logic_1164.all;
use ieee.std_logic_unsigned.all;
use ieee.std_logic_arith.all;

ENTITY convertor_bin_dec_ore IS
  PORT (
bin:in std_logic_vector(4 downto 0);
  	   zec:out std_logic_vector(3 downto 0);
  	   uni:out std_logic_vector(3 downto 0));
END convertor_bin_dec_ore;


ARCHITECTURE TypeArchitecture OF convertor_bin_dec_ore IS

signal numar:integer:=0;
signal z,u:integer:=0;

BEGIN

numar<=conv_integer(bin);
z<=numar/10;
u<=numar rem 10;

process(z)
begin
	case z is
		when 0 => zec <=x"0";
		when 1 => zec <=x"1";
		when 2 => zec <=x"2";
		when 3 => zec <=x"3";
		when 4 => zec <=x"4";
		when 5 => zec <=x"5";
		when 6 => zec <=x"6";
		when 7 => zec <=x"7";
		when 8 => zec <=x"8";
		when 9 => zec <=x"9";
		when others => zec <=x"f";
	end case;
end process;

process(u)
begin
	case u is
		when 0 => uni <=x"0";
		when 1 => uni <=x"1";
		when 2 => uni <=x"2";
		when 3 => uni <=x"3";
		when 4 => uni <=x"4";
		when 5 => uni <=x"5";
		when 6 => uni <=x"6";
		when 7 => uni <=x"7";
		when 8 => uni <=x"8";
		when 9 => uni <=x"9";
		when others => uni <=x"f";
	end case;
end process;
	

END TypeArchitecture;
